// Logisim project XOR.circ as structural Verilog: 2 circuits, main circuit main
module main (
  input  X,
  input  Y,
  input  in_3,
  input  in_4,
  input  in_5,
  input  in_6,
  input  in_7,
  input  in_8,
  output S,
  output out_10
);

  wire AND_1_out, AND_2_out, mux2x1_1_out_4, mux2x1_2_out_4, not_1_out, not_2_out;

  not not_1 (not_1_out, X);
  not not_2 (not_2_out, Y);
  and AND_1 (AND_1_out, not_1_out, Y);
  and AND_2 (AND_2_out, X, not_2_out);
  mux2x1 mux2x1_1 (.A(in_3), .B(in_4), .S(in_7), .out_4(mux2x1_1_out_4));
  mux2x1 mux2x1_2 (.A(in_5), .B(in_6), .S(in_7), .out_4(mux2x1_2_out_4));
  or OR (S, AND_1_out, AND_2_out);
  mux2x1 mux2x1_3 (.A(mux2x1_1_out_4), .B(mux2x1_2_out_4), .S(in_8), .out_4(out_10));

  // Notes on the sheet:
  //   XOR Circuit
endmodule

module mux2x1 (
  input  A,
  input  B,
  input  S,
  output out_4
);

  wire and_1_out, and_2_out, not_1_out;

  not not_1 (not_1_out, S);
  and and_1 (and_1_out, A, not_1_out);
  and and_2 (and_2_out, B, S);
  or or_1 (out_4, and_1_out, and_2_out);
endmodule
